# Fritzing sketch ColorDance - Sketch (saved by Fritzing 0.9.10b)
breadboards: 1

parts:
  Part1 = Arduino Uno (Rev3) - ICSP
  LED1 = LEDs [package=led10mm]
  LED2 = LEDs [package=led10mm]
  LED3 = LEDs [package=led10mm]
  LED4 = LEDs [package=led10mm]

nets:
  N1: Part1.GND, LED1.C, LED2.C, LED3.C
  N2: Part1.D0/RX, LED1.A
  N3: Part1.D1/TX, LED2.A
  N4: Part1.D2, LED3.A
  N5: Part1.D3_PWM, LED4.A
