# Fritzing sketch PushButton Sketch (saved by Fritzing 0.9.10b)
breadboards: 1

parts:
  Part1 = Arduino Uno (Rev3) - ICSP
  LED1 = LED - 3mm [color="Red (633nm)" current=0.030 package="3 mm [THT]"]
  S1 = SWITCH-MOMENTARY-2 [package=tactile_switch_smd-2]
  S2 = SWITCH-MOMENTARY-2 [package=tactile_switch_smd-2]

nets:
  N1: Part1.D8, LED1.anode
  N2: Part1.D2, S1.2
  N3: Part1.D3_PWM, S2.2
  N4: Part1.GND, LED1.cathode
